// Logisim project 2-bit half adder.circ as structural Verilog: 1 circuit, main circuit main
module main (
  input  Ci,
  input  A0,
  input  B0,
  input  A1,
  input  B1
);

  wire and_1_out, and_2_out, and_3_out, and_4_out, and_5_out, and_6_out, and_7_out, and_8_out, or_1_out,
       or_2_out, or_3_out, or_4_out, xor_1_out, xor_2_out;

  and and_1 (and_1_out, B0, A0);
  and and_2 (and_2_out, B1, A1);
  and and_3 (and_3_out, Ci, A0);
  or or_1 (or_1_out, and_1_out, and_3_out, and_5_out, and_7_out);
  and and_4 (and_4_out, B1, or_1_out);
  or or_2 (or_2_out, and_2_out, and_4_out, and_6_out);
  LED Co (.in(or_2_out));
  and and_5 (and_5_out, B0, Ci);
  and and_6 (and_6_out, or_1_out, A1);
  and and_7 (and_7_out, Ci, A0, B0);
  and and_8 (and_8_out, B1, A1, or_1_out);
  ExactlyOne xor_1 (.out(xor_1_out), .in0(Ci), .in1(A0), .in4(B0));
  ExactlyOne xor_2 (.out(xor_2_out), .in0(or_1_out), .in2(A1), .in4(B1));
  or or_3 (or_3_out, and_8_out, xor_2_out);
  LED S1 (.in(or_3_out));
  or or_4 (or_4_out, and_7_out, xor_1_out);
  LED S0 (.in(or_4_out));

  // Notes on the sheet:
  //   Co
  //   Carry Line
  //   S1
  //   S0
endmodule
